// Logisim project finalcircuit.circ as structural Verilog: 28 circuits, main circuit main
module main (
);

  wire ALU_zero, button_1_out, button_2_out, clock_1_out, data_hazard_1_or_out, Decoder_halt,
       Decoder_immtoalu, Decoder_immtopc, Decoder_led, Decoder_memread, Decoder_memtoreg, Decoder_memwrite,
       Decoder_regtopc, Decoder_regwrite, Decoder_sub, Decoder_writeled, Decoder_zerostoalu,
       ex_mem_1_memread_2, ex_mem_1_memtoreg_2, ex_mem_1_memwrite_2, ex_mem_1_regenable_2,
       ex_mem_1_regwrite_2, ex_mem_1_writele, id_ex_1_immtoalu_2, id_ex_1_memread_2, id_ex_1_memtoreg_2,
       id_ex_1_memwrite_2, id_ex_1_regenable_2, id_ex_1_regwrite_2, id_ex_1_sub_2, id_ex_1_writeled_2,
       id_ex_1_zeroestopc_2, if_id_1_p2, if_id_1_p10, Instruction_Splitter_subop,
       Instruction_Splitter_unsigned, mem_wb_1_memtoreg_2, mem_wb_1_regwrite_2, mem_wb_1_writeled_2,
       multiplexer_3_out, not_1_out, or_1_out, regWriteSelect_out_3, ResultToLess_less;
  wire [1:0] Forwarding_Unit_controla, Forwarding_Unit_controlb;
  wire [2:0] ex_mem_1_rr1_rd_2, id_ex_1_rr1_2, Instruction_Splitter_readregister1,
       Instruction_Splitter_readregister2, mem_wb_1_rd_rs_2;
  wire [3:0] Decoder_aluop, id_ex_1_aluop_2, Instruction_Splitter_opcode;
  wire [7:0] adder_1_out, if_id_1_p9, if_id_1_p11, Instruction_Splitter_immediate, PC_q, pcselect_1_out_6,
       RegistertoAddress_address;
  wire [15:0] ALU_result, ALU_sub, data_hazard_1_mux_out, ex_mem_1_alu_result_2, ex_mem_1_putvalue_2,
       ex_mem_1_write_data_2, id_ex_1_rd1_2, id_ex_1_rd2_2, id_ex_1_sign_extend_2, if_id_1_p12,
       mem_wb_1_address_2, mem_wb_1_putvalue, mem_wb_1_read_data_2, multiplexer_1_out, multiplexer_2_out,
       multiplexer_4_out, multiplexer_5_out, multiplexer_6_out, multiplexer_7_out, multiplexer_8_out,
       ram_1_data, register_1_q, Registers_readdata1, Registers_readdata2, rom_1_data,
       Sign_Extend_signextendedimm;

  Clock clock_1 (.out(clock_1_out));
  not not_1 (not_1_out, Decoder_halt);
  Register PC (.D(pcselect_1_out_6), .en(data_hazard_1_or_out), .Q(PC_q), .clk(clock_1_out), .clr(button_1_out));
  Button button_1 (.out(button_1_out));
  Data_Hazard data_hazard_1 (
    .inst(rom_1_data), .clock(clock_1_out), .halt(Decoder_halt), .or_out(data_hazard_1_or_out),
    .mux_out(data_hazard_1_mux_out));
  Adder adder_1 (.a(PC_q), .b(8'h1), .out(adder_1_out));  // open: cin, cout
  Button button_2 (.out(button_2_out));
  Multiplexer #(.select(2), .width(16), .enable("false")) multiplexer_1 (
    .in0(Registers_readdata1), .in1(multiplexer_8_out), .in2(multiplexer_7_out), .out(multiplexer_1_out),
    .sel(Forwarding_Unit_controla));  // open: in3
  ROM #(.dataWidth(16)) rom_1 (.addr(PC_q), .data(rom_1_data), .sel(1'b1));
  Multiplexer #(.select(2), .width(16), .enable("false")) multiplexer_2 (
    .in0(Registers_readdata2), .in1(multiplexer_8_out), .in2(multiplexer_7_out), .out(multiplexer_2_out),
    .sel(Forwarding_Unit_controlb));  // open: in3
  regWriteReset regWriteSelect (.in_1(adder_1_out), .in_2(if_id_1_p9), .out_3(regWriteSelect_out_3));
  // IF_ID if_id_1: pin names not known; wires that end beside it: data_hazard_1_or_out, if_id_1_p2, if_id_1_p2, PC_q, data_hazard_1_mux_out, button_2_out, not_1_out, clock_1_out, if_id_1_p9, if_id_1_p10, if_id_1_p11, if_id_1_p12
  InstructionSplitter Instruction_Splitter (
    .Instruction(if_id_1_p12), .Opcode(Instruction_Splitter_opcode),
    .ReadRegister1(Instruction_Splitter_readregister1), .ReadRegister2(Instruction_Splitter_readregister2),
    .SubOp(Instruction_Splitter_subop), .Unsigned(Instruction_Splitter_unsigned),
    .Immediate(Instruction_Splitter_immediate));  // open: WriteRegister, ShiftAmount
  ResultToLess ResultToLess (.Result(ALU_result), .Less(ResultToLess_less));
  Multiplexer #(.enable("false")) multiplexer_3 (
    .in0(Decoder_regwrite), .in1(1'b0), .out(multiplexer_3_out), .sel(regWriteSelect_out_3));
  pcSelect pcselect_1 (
    .PC_1(adder_1_out), .immediate(Instruction_Splitter_immediate), .rd1(Registers_readdata1),
    .IMMTOPC(Decoder_immtopc), .REGTOPC(Decoder_regtopc), .out_6(pcselect_1_out_6));
  SignExtend Sign_Extend (
    .Unsigned(Instruction_Splitter_unsigned), .Immediate(Instruction_Splitter_immediate),
    .SignExtendedImm(Sign_Extend_signextendedimm));
  Decoder Decoder (
    .Opcode(Instruction_Splitter_opcode), .Subop(Instruction_Splitter_subop), .Zero(ALU_zero),
    .Less(ResultToLess_less), .RegWrite(Decoder_regwrite), .ALUOp(Decoder_aluop),
    .IMMtoALU(Decoder_immtoalu), .RegtoPC(Decoder_regtopc), .IMMtoPC(Decoder_immtopc),
    .ZerosToALU(Decoder_zerostoalu), .MemWrite(Decoder_memwrite), .MemtoReg(Decoder_memtoreg),
    .Halt(Decoder_halt), .LED(Decoder_led), .WriteLED(Decoder_writeled), .MemRead(Decoder_memread),
    .Sub(Decoder_sub));  // open: ShiftSrc, ShifterToReg, PCtoReg
  RegisterFile Registers (
    .ReadRegister1(Instruction_Splitter_readregister1), .ReadRegister2(Instruction_Splitter_readregister2),
    .WriteRegister(mem_wb_1_rd_rs_2), .WriteData(multiplexer_8_out), .WriteEnable(mem_wb_1_regwrite_2),
    .Clock(clock_1_out), .ReadData1(Registers_readdata1), .ReadData2(Registers_readdata2));
  ID_EX id_ex_1 (
    .PC(if_id_1_p11), .rd1(multiplexer_1_out), .rd2(multiplexer_2_out),
    .sign_extend(Sign_Extend_signextendedimm), .rr1(Instruction_Splitter_readregister1),
    .ALUOp(Decoder_aluop), .rd1_2(id_ex_1_rd1_2), .rd2_2(id_ex_1_rd2_2),
    .sign_extend_2(id_ex_1_sign_extend_2), .rr1_2(id_ex_1_rr1_2), .ALUOp_2(id_ex_1_aluop_2),
    .clock(clock_1_out), .PC_1(if_id_1_p9), .regEnable(if_id_1_p10), .regEnable_2(id_ex_1_regenable_2),
    .IMMTOALU(Decoder_immtoalu), .IMMTOALU_2(id_ex_1_immtoalu_2), .REGTOPC(Decoder_regtopc),
    .IMMTOPC(Decoder_immtopc), .ZEROESTOPC(Decoder_zerostoalu), .ZEROESTOPC_2(id_ex_1_zeroestopc_2),
    .MEMWRITE(Decoder_memwrite), .MEMWRITE_2(id_ex_1_memwrite_2), .MEMTOREG(Decoder_memtoreg),
    .MEMTOREG_2(id_ex_1_memtoreg_2), .WRITELED(Decoder_writeled), .WRITELED_2(id_ex_1_writeled_2),
    .MEMREAD(Decoder_memread), .MEMREAD_2(id_ex_1_memread_2), .REGWRITE(multiplexer_3_out),
    .REGWRITE_2(id_ex_1_regwrite_2), .SUB(Decoder_sub), .SUB_2(id_ex_1_sub_2), .enable(if_id_1_p10),
    .rr2(Instruction_Splitter_readregister2));  // open: PC_2, PC_1_2, REGTOPC_2, IMMTOPC_2, reset, rr2_2
  LED Halt (.in(Decoder_led));
  Multiplexer #(.width(16), .disabled(0), .enable("false")) multiplexer_4 (
    .in0(id_ex_1_rd2_2), .in1(id_ex_1_sign_extend_2), .out(multiplexer_4_out), .sel(id_ex_1_immtoalu_2));
  Multiplexer #(.width(16), .disabled(0), .enable("false")) multiplexer_5 (
    .in0(multiplexer_4_out), .in1({16{1'b0}}), .out(multiplexer_5_out), .sel(id_ex_1_zeroestopc_2));
  sixteen_bit_ALU ALU (
    .ALUOperation(id_ex_1_aluop_2), .a(id_ex_1_rd1_2), .b(multiplexer_5_out), .Zero(ALU_zero),
    .Result(ALU_result), .sub(ALU_sub));  // open: Overflow
  or or_1 (or_1_out, id_ex_1_memwrite_2, id_ex_1_memtoreg_2);
  Forwarding_Unit Forwarding_Unit (
    .EX_MEM_registerRd(id_ex_1_rr1_2), .MEM_WB_registerRd(mem_wb_1_rd_rs_2),
    .ID_EX_registerRs1(Instruction_Splitter_readregister1),
    .ID_EX_registerRs2(Instruction_Splitter_readregister2), .EX_MEM_regWrite(id_ex_1_regwrite_2),
    .MEM_WB_regWrite(ex_mem_1_regwrite_2), .controlB(Forwarding_Unit_controlb),
    .controlA(Forwarding_Unit_controla));
  Multiplexer #(.width(16), .enable("false")) multiplexer_6 (
    .in0(ALU_result), .in1(ALU_sub), .out(multiplexer_6_out), .sel(id_ex_1_sub_2));
  Multiplexer #(.width(16), .enable("false")) multiplexer_7 (
    .in0(multiplexer_6_out), .in1(multiplexer_5_out), .out(multiplexer_7_out), .sel(or_1_out));
  EX_MEM ex_mem_1 (
    .putValue(id_ex_1_rd1_2), .ALU_result(multiplexer_7_out), .write_data(id_ex_1_rd1_2),
    .rr1_rd(id_ex_1_rr1_2), .putValue_2(ex_mem_1_putvalue_2), .ALU_result_2(ex_mem_1_alu_result_2),
    .write_data_2(ex_mem_1_write_data_2), .rr1_rd_2(ex_mem_1_rr1_rd_2), .clock(clock_1_out),
    .MEMWRITE(id_ex_1_memwrite_2), .MEMWRITE_2(ex_mem_1_memwrite_2), .MEMTOREG(id_ex_1_memtoreg_2),
    .MEMTOREG_2(ex_mem_1_memtoreg_2), .MEMREAD(id_ex_1_memread_2), .MEMREAD_2(ex_mem_1_memread_2),
    .REGWRITE(id_ex_1_regwrite_2), .REGWRITE_2(ex_mem_1_regwrite_2), .enable(id_ex_1_regenable_2),
    .regEnable(id_ex_1_regenable_2), .regEnable_2(ex_mem_1_regenable_2), .writeLED(id_ex_1_writeled_2),
    .writeLE(ex_mem_1_writele));
  ALUtoPC RegistertoAddress (.ALUOut(ex_mem_1_alu_result_2), .Address(RegistertoAddress_address));
  RAM #(.dataWidth(16), .bus("separate")) ram_1 (
    .addr(RegistertoAddress_address), .din(ex_mem_1_write_data_2), .data(ram_1_data),
    .str(ex_mem_1_memwrite_2), .sel(1'b1), .clk(clock_1_out), .ld(ex_mem_1_memread_2));  // open: clr
  MEM_WB mem_wb_1 (
    .read_data(ram_1_data), .address(ex_mem_1_alu_result_2), .rd_rs(ex_mem_1_rr1_rd_2),
    .read_data_2(mem_wb_1_read_data_2), .address_2(mem_wb_1_address_2), .rd_rs_2(mem_wb_1_rd_rs_2),
    .clock(clock_1_out), .MEMTOREG(ex_mem_1_memtoreg_2), .MEMTOREG_2(mem_wb_1_memtoreg_2),
    .REGWRITE(ex_mem_1_regwrite_2), .REGWRITE_2(mem_wb_1_regwrite_2), .enable(ex_mem_1_regenable_2),
    .writeLED(ex_mem_1_writele), .writeLED_2(mem_wb_1_writeled_2), .putvalue(mem_wb_1_putvalue),
    .put_value(ex_mem_1_putvalue_2));  // open: reset
  Multiplexer #(.width(16), .disabled(0), .enable("false")) multiplexer_8 (
    .in0(mem_wb_1_address_2), .in1(mem_wb_1_read_data_2), .out(multiplexer_8_out), .sel(mem_wb_1_memtoreg_2));
  Hex_Digit_Display hex_digit_display_1 (.value(register_1_q[15:12]));  // open: dp
  Register #(.width(16)) register_1 (
    .D(mem_wb_1_putvalue), .en(mem_wb_1_writeled_2), .Q(register_1_q), .clk(clock_1_out));  // open: clr
  Hex_Digit_Display hex_digit_display_2 (.value(register_1_q[11:8]));  // open: dp
  Hex_Digit_Display hex_digit_display_3 (.value(register_1_q[7:4]));  // open: dp
  Hex_Digit_Display hex_digit_display_4 (.value(register_1_q[3:0]));  // open: dp

  // Notes on the sheet:
  //   contents of rom_1 (hex, n*v repeats v):
  //   280 8603 1402 1904 a206 1c06 1a07 f400 f200 f600 fc00 7000
endmodule

module InstructionSplitter (
  input  [15:0] Instruction,
  output [3:0] Opcode,
  output [2:0] ReadRegister1,
  output [2:0] ReadRegister2,
  output [2:0] WriteRegister,
  output [3:0] ShiftAmount,
  output SubOp,
  output Unsigned,
  output [7:0] Immediate
);


  assign Immediate = Instruction[7:0];
  assign Opcode = Instruction[15:12];
  assign ReadRegister1 = Instruction[11:9];
  assign ReadRegister2 = Instruction[8:6];
  assign ShiftAmount = Instruction[4:1];
  assign SubOp = Instruction[0];
  assign Unsigned = Instruction[8];
  assign WriteRegister = Instruction[11:9];
endmodule

module SignExtend (
  input  Unsigned,
  input  [7:0] Immediate,
  output [15:0] SignExtendedImm
);

  wire [15:0] bit_extender_1_out, bit_extender_2_out;

  assign bit_extender_1_out = {{8{Immediate[7]}}, Immediate};  // Bit_Extender bit_extender_1
  assign bit_extender_2_out = {{8{1'b0}}, Immediate};  // Bit_Extender bit_extender_2
  Multiplexer #(.width(16), .disabled(0), .enable("false")) multiplexer_1 (
    .in0(bit_extender_1_out), .in1(bit_extender_2_out), .out(SignExtendedImm), .sel(Unsigned));
endmodule

module ALUtoPC (
  input  [15:0] ALUOut,
  output [7:0] Address
);


  assign Address = ALUOut[7:0];
endmodule

module Shifter (
  input  Subop,
  input  [15:0] Data,
  input  [15:0] ShamtReg,
  input  ShiftSrc,
  input  [3:0] Shamt,
  output [15:0] ShiftOut
);

  wire [3:0] multiplexer_1_out;
  wire [15:0] shifter_1_out, shifter_2_out;

  Multiplexer #(.width(4), .disabled(0), .enable("false")) multiplexer_1 (
    .in0(ShamtReg[3:0]), .in1(Shamt), .out(multiplexer_1_out), .sel(ShiftSrc));
  Shifter_part #(.width(16)) shifter_1 (.in(Data), .\dist (multiplexer_1_out), .out(shifter_1_out));
  Shifter_part #(.width(16), .shift("lr")) shifter_2 (.in(Data), .\dist (multiplexer_1_out), .out(shifter_2_out));
  Multiplexer #(.width(16), .disabled(0), .enable("false")) multiplexer_2 (
    .in0(shifter_1_out), .in1(shifter_2_out), .out(ShiftOut), .sel(Subop));
endmodule

module RegisterFile (
  input  [2:0] ReadRegister1,
  input  [2:0] ReadRegister2,
  input  [2:0] WriteRegister,
  input  [15:0] WriteData,
  input  WriteEnable,
  input  Clock,
  output [15:0] ReadData1,
  output [15:0] ReadData2
);

  wire decoder_1_out0, decoder_1_out1, decoder_1_out2, decoder_1_out3, decoder_1_out4, decoder_1_out5,
       decoder_1_out6, decoder_1_out7;
  wire [15:0] register_1_q, register_2_q, register_3_q, register_4_q, register_5_q, register_6_q,
       register_7_q, register_8_q;

  Decoder_part #(.select(3), .disabled(0)) decoder_1 (
    .out0(decoder_1_out0), .out1(decoder_1_out1), .out2(decoder_1_out2), .out3(decoder_1_out3),
    .out4(decoder_1_out4), .out5(decoder_1_out5), .out6(decoder_1_out6), .out7(decoder_1_out7),
    .sel(WriteRegister), .en(WriteEnable));
  Register #(.width(16)) register_1 (.D(WriteData), .en(decoder_1_out0), .Q(register_1_q), .clk(Clock));  // open: clr
  Register #(.width(16)) register_2 (.D(WriteData), .en(decoder_1_out1), .Q(register_2_q), .clk(Clock));  // open: clr
  Register #(.width(16)) register_3 (.D(WriteData), .en(decoder_1_out2), .Q(register_3_q), .clk(Clock));  // open: clr
  Register #(.width(16)) register_4 (.D(WriteData), .en(decoder_1_out3), .Q(register_4_q), .clk(Clock));  // open: clr
  Register #(.width(16)) register_5 (.D(WriteData), .en(decoder_1_out4), .Q(register_5_q), .clk(Clock));  // open: clr
  Register #(.width(16)) register_6 (.D(WriteData), .en(decoder_1_out5), .Q(register_6_q), .clk(Clock));  // open: clr
  Register #(.width(16)) register_7 (.D(WriteData), .en(decoder_1_out6), .Q(register_7_q), .clk(Clock));  // open: clr
  Register #(.width(16)) register_8 (.D(WriteData), .en(decoder_1_out7), .Q(register_8_q), .clk(Clock));  // open: clr
  Multiplexer #(.select(3), .width(16), .enable("false")) multiplexer_1 (
    .in0(register_1_q), .in1(register_2_q), .in2(register_3_q), .in3(register_4_q), .in4(register_5_q),
    .in5(register_6_q), .in6(register_7_q), .in7(register_8_q), .out(ReadData1), .sel(ReadRegister1));
  Multiplexer #(.select(3), .width(16), .enable("false")) multiplexer_2 (
    .in0(register_1_q), .in1(register_2_q), .in2(register_3_q), .in3(register_4_q), .in4(register_5_q),
    .in5(register_6_q), .in6(register_7_q), .in7(register_8_q), .out(ReadData2), .sel(ReadRegister2));
endmodule

module ShifterDecoder (
  input  [3:0] Opcode,
  output ShiftSrc,
  output ShiftertoReg,
  output RegWrite
);

  and and_1 (RegWrite, ~Opcode[3], Opcode[2], ~Opcode[1]);  // AND_Gate

  assign ShiftertoReg = RegWrite;
  assign ShiftSrc = Opcode[0];
endmodule

module Arith_Log_Decoder (
  input  [3:0] Opcode,
  input  Subop,
  output [3:0] ALUOperation,
  output RegWrite,
  output ALUSrc
);

  wire and_2_out, and_3_out, and_5_out, and_6_out, not_1_out, not_2_out, not_3_out, not_4_out, not_5_out,
       not_6_out, not_7_out, not_8_out, not_9_out, not_10_out, not_11_out, not_12_out, not_13_out,
       not_14_out, not_15_out, not_16_out, not_17_out, not_18_out, not_19_out, not_20_out, not_21_out;

  not not_1 (not_1_out, Opcode[3]);
  not not_2 (not_2_out, Opcode[2]);
  not not_3 (not_3_out, Subop);
  not not_4 (not_4_out, Opcode[3]);
  not not_5 (not_5_out, Opcode[2]);
  not not_6 (not_6_out, Opcode[1]);
  not not_7 (not_7_out, Opcode[0]);
  not not_8 (not_8_out, Opcode[3]);
  not not_9 (not_9_out, Opcode[2]);
  not not_10 (not_10_out, Subop);
  not not_11 (not_11_out, Opcode[3]);
  not not_12 (not_12_out, Opcode[2]);
  not not_13 (not_13_out, Opcode[1]);
  not not_14 (not_14_out, Opcode[3]);
  not not_15 (not_15_out, Opcode[2]);
  not not_16 (not_16_out, Opcode[1]);
  not not_17 (not_17_out, Opcode[3]);
  not not_18 (not_18_out, Opcode[2]);
  not not_19 (not_19_out, Opcode[3]);
  not not_20 (not_20_out, Opcode[2]);
  not not_21 (not_21_out, Opcode[1]);
  and and_1 (ALUOperation[3], not_1_out, not_2_out, Opcode[1], Opcode[0], not_3_out);
  and and_2 (and_2_out, not_4_out, not_5_out, not_6_out, not_7_out, Subop);
  and and_3 (and_3_out, not_8_out, not_9_out, Opcode[1], Opcode[0], not_10_out);
  and and_4 (ALUOperation[1], not_11_out, not_12_out, not_13_out);
  and and_5 (and_5_out, not_14_out, not_15_out, not_16_out);
  and and_6 (and_6_out, not_17_out, not_18_out, Opcode[0]);
  and and_7 (ALUSrc, not_19_out, not_20_out, not_21_out, Opcode[0]);
  or or_1 (ALUOperation[2], and_2_out, and_3_out);
  or or_2 (RegWrite, and_5_out, and_6_out);

  assign ALUOperation[0] = 1'b0;
endmodule

module Arith_Log (
  input  Opcode3,
  input  Opcode2,
  input  Opcode1,
  input  Opcode0,
  input  Unsigned,
  input  Subop,
  output ALUOp3,
  output ALUOp2,
  output ALUOp1,
  output ALUOp0,
  output RegWrite,
  output ALUSrc
);

  wire and_2_out, and_3_out, and_5_out, and_6_out, not_1_out, not_2_out, not_3_out, not_4_out, not_5_out,
       not_6_out, not_7_out, not_8_out, not_9_out, not_10_out, not_11_out, not_12_out, not_13_out,
       not_14_out, not_15_out, not_16_out, not_17_out, not_18_out, not_19_out, not_20_out, not_21_out;

  not not_1 (not_1_out, Opcode3);
  not not_2 (not_2_out, Opcode2);
  not not_3 (not_3_out, Subop);
  not not_4 (not_4_out, Opcode3);
  not not_5 (not_5_out, Opcode2);
  not not_6 (not_6_out, Opcode1);
  not not_7 (not_7_out, Opcode0);
  not not_8 (not_8_out, Opcode3);
  not not_9 (not_9_out, Opcode2);
  not not_10 (not_10_out, Subop);
  not not_11 (not_11_out, Opcode3);
  not not_12 (not_12_out, Opcode2);
  not not_13 (not_13_out, Opcode1);
  not not_14 (not_14_out, Opcode3);
  not not_15 (not_15_out, Opcode2);
  not not_16 (not_16_out, Opcode1);
  not not_17 (not_17_out, Opcode3);
  not not_18 (not_18_out, Opcode2);
  not not_19 (not_19_out, Opcode3);
  not not_20 (not_20_out, Opcode2);
  not not_21 (not_21_out, Opcode1);
  and and_1 (ALUOp3, not_1_out, not_2_out, Opcode1, Opcode0, not_3_out);
  and and_2 (and_2_out, not_4_out, not_5_out, not_6_out, not_7_out, Subop);
  and and_3 (and_3_out, not_8_out, not_9_out, Opcode1, Opcode0, not_10_out);
  and and_4 (ALUOp1, not_11_out, not_12_out, not_13_out);
  and and_5 (and_5_out, not_14_out, not_15_out, not_16_out);
  and and_6 (and_6_out, not_17_out, not_18_out, Opcode0);
  and and_7 (ALUSrc, not_19_out, not_20_out, not_21_out, Opcode0);
  or or_1 (ALUOp2, and_2_out, and_3_out);
  or or_2 (RegWrite, and_5_out, and_6_out);

  assign ALUOp0 = 1'b0;
endmodule

module one_bit_ALU (
  input  Ainvert,
  input  Binvert,
  input  CarryIn,
  input  [1:0] Operation,
  input  a,
  input  b,
  input  Less,
  output Result,
  output Set,
  output CarryOut
);

  wire and_1_out, multiplexer_1_out, multiplexer_2_out, not_1_out, not_2_out, or_1_out;

  not not_1 (not_1_out, a);
  Multiplexer #(.enable("false")) multiplexer_1 (.in0(a), .in1(not_1_out), .out(multiplexer_1_out), .sel(Ainvert));
  not not_2 (not_2_out, b);
  Multiplexer #(.enable("false")) multiplexer_2 (.in0(b), .in1(not_2_out), .out(multiplexer_2_out), .sel(Binvert));
  and and_1 (and_1_out, multiplexer_1_out, multiplexer_2_out);
  or or_1 (or_1_out, multiplexer_1_out, multiplexer_2_out);
  Adder #(.width(1)) adder_1 (.a(multiplexer_1_out), .b(multiplexer_2_out), .out(Set), .cin(CarryIn), .cout(CarryOut));
  Multiplexer #(.select(2), .enable("false")) multiplexer_3 (
    .in0(and_1_out), .in1(or_1_out), .in2(Set), .in3(Less), .out(Result), .sel(Operation));
endmodule

module sixteen_bit_ALU (
  input  [3:0] ALUOperation,
  input  [15:0] a,
  input  [15:0] b,
  output Zero,
  output [15:0] Result,
  output Overflow,
  output [15:0] sub
);

  wire one_bit_alu_1_carryout, one_bit_alu_2_carryout, one_bit_alu_3_carryout, one_bit_alu_4_carryout,
       one_bit_alu_5_carryout, one_bit_alu_6_carryout, one_bit_alu_7_carryout, one_bit_alu_8_carryout,
       one_bit_alu_9_carryout, one_bit_alu_10_carryout, one_bit_alu_11_carryout, one_bit_alu_12_carryout,
       one_bit_alu_13_carryout, one_bit_alu_14_carryout, one_bit_alu_15_carryout, one_bit_alu_16_carryout,
       one_bit_alu_16_set, xor_1_out;

  one_bit_ALU one_bit_alu_1 (
    .a(a[0]), .b(b[0]), .Less(xor_1_out), .Ainvert(ALUOperation[3]), .Binvert(ALUOperation[2]),
    .CarryIn(ALUOperation[2]), .Operation(ALUOperation[1:0]), .CarryOut(one_bit_alu_1_carryout),
    .Result(Result[0]));  // open: Set
  one_bit_ALU one_bit_alu_2 (
    .a(a[1]), .b(b[1]), .Less(1'b0), .Ainvert(ALUOperation[3]), .Binvert(ALUOperation[2]),
    .CarryIn(one_bit_alu_1_carryout), .Operation(ALUOperation[1:0]), .CarryOut(one_bit_alu_2_carryout),
    .Result(Result[1]));  // open: Set
  one_bit_ALU one_bit_alu_3 (
    .a(a[2]), .b(b[2]), .Less(1'b0), .Ainvert(ALUOperation[3]), .Binvert(ALUOperation[2]),
    .CarryIn(one_bit_alu_2_carryout), .Operation(ALUOperation[1:0]), .CarryOut(one_bit_alu_3_carryout),
    .Result(Result[2]));  // open: Set
  one_bit_ALU one_bit_alu_4 (
    .a(a[3]), .b(b[3]), .Less(1'b0), .Ainvert(ALUOperation[3]), .Binvert(ALUOperation[2]),
    .CarryIn(one_bit_alu_3_carryout), .Operation(ALUOperation[1:0]), .CarryOut(one_bit_alu_4_carryout),
    .Result(Result[3]));  // open: Set
  one_bit_ALU one_bit_alu_5 (
    .a(a[4]), .b(b[4]), .Less(1'b0), .Ainvert(ALUOperation[3]), .Binvert(ALUOperation[2]),
    .CarryIn(one_bit_alu_4_carryout), .Operation(ALUOperation[1:0]), .CarryOut(one_bit_alu_5_carryout),
    .Result(Result[4]));  // open: Set
  one_bit_ALU one_bit_alu_6 (
    .a(a[5]), .b(b[5]), .Less(1'b0), .Ainvert(ALUOperation[3]), .Binvert(ALUOperation[2]),
    .CarryIn(one_bit_alu_5_carryout), .Operation(ALUOperation[1:0]), .CarryOut(one_bit_alu_6_carryout),
    .Result(Result[5]));  // open: Set
  one_bit_ALU one_bit_alu_7 (
    .a(a[6]), .b(b[6]), .Less(1'b0), .Ainvert(ALUOperation[3]), .Binvert(ALUOperation[2]),
    .CarryIn(one_bit_alu_6_carryout), .Operation(ALUOperation[1:0]), .CarryOut(one_bit_alu_7_carryout),
    .Result(Result[6]));  // open: Set
  one_bit_ALU one_bit_alu_8 (
    .a(a[7]), .b(b[7]), .Less(1'b0), .Ainvert(ALUOperation[3]), .Binvert(ALUOperation[2]),
    .CarryIn(one_bit_alu_7_carryout), .Operation(ALUOperation[1:0]), .CarryOut(one_bit_alu_8_carryout),
    .Result(Result[7]));  // open: Set
  one_bit_ALU one_bit_alu_9 (
    .a(a[8]), .b(b[8]), .Less(1'b0), .Ainvert(ALUOperation[3]), .Binvert(ALUOperation[2]),
    .CarryIn(one_bit_alu_8_carryout), .Operation(ALUOperation[1:0]), .CarryOut(one_bit_alu_9_carryout),
    .Result(Result[8]));  // open: Set
  one_bit_ALU one_bit_alu_10 (
    .a(a[9]), .b(b[9]), .Less(1'b0), .Ainvert(ALUOperation[3]), .Binvert(ALUOperation[2]),
    .CarryIn(one_bit_alu_9_carryout), .Operation(ALUOperation[1:0]), .CarryOut(one_bit_alu_10_carryout),
    .Result(Result[9]));  // open: Set
  one_bit_ALU one_bit_alu_11 (
    .a(a[10]), .b(b[10]), .Less(1'b0), .Ainvert(ALUOperation[3]), .Binvert(ALUOperation[2]),
    .CarryIn(one_bit_alu_10_carryout), .Operation(ALUOperation[1:0]), .CarryOut(one_bit_alu_11_carryout),
    .Result(Result[10]));  // open: Set
  one_bit_ALU one_bit_alu_12 (
    .a(a[11]), .b(b[11]), .Less(1'b0), .Ainvert(ALUOperation[3]), .Binvert(ALUOperation[2]),
    .CarryIn(one_bit_alu_11_carryout), .Operation(ALUOperation[1:0]), .CarryOut(one_bit_alu_12_carryout),
    .Result(Result[11]));  // open: Set
  one_bit_ALU one_bit_alu_13 (
    .a(a[12]), .b(b[12]), .Less(1'b0), .Ainvert(ALUOperation[3]), .Binvert(ALUOperation[2]),
    .CarryIn(one_bit_alu_12_carryout), .Operation(ALUOperation[1:0]), .CarryOut(one_bit_alu_13_carryout),
    .Result(Result[12]));  // open: Set
  one_bit_ALU one_bit_alu_14 (
    .a(a[13]), .b(b[13]), .Less(1'b0), .Ainvert(ALUOperation[3]), .Binvert(ALUOperation[2]),
    .CarryIn(one_bit_alu_13_carryout), .Operation(ALUOperation[1:0]), .CarryOut(one_bit_alu_14_carryout),
    .Result(Result[13]));  // open: Set
  one_bit_ALU one_bit_alu_15 (
    .a(a[14]), .b(b[14]), .Less(1'b0), .Ainvert(ALUOperation[3]), .Binvert(ALUOperation[2]),
    .CarryIn(one_bit_alu_14_carryout), .Operation(ALUOperation[1:0]), .CarryOut(one_bit_alu_15_carryout),
    .Result(Result[14]));  // open: Set
  one_bit_ALU one_bit_alu_16 (
    .a(a[15]), .b(b[15]), .Less(1'b0), .Ainvert(ALUOperation[3]), .Binvert(ALUOperation[2]),
    .CarryIn(one_bit_alu_15_carryout), .Operation(ALUOperation[1:0]), .CarryOut(one_bit_alu_16_carryout),
    .Result(Result[15]), .Set(one_bit_alu_16_set));
  xor xor_1 (xor_1_out, one_bit_alu_16_set, Overflow);
  xor xor_2 (Overflow, one_bit_alu_15_carryout, one_bit_alu_16_carryout);
  Subtractor #(.width(16)) subtractor_1 (.a(a), .b(b), .out(sub));  // open: bin, bout
  nor nor_1 (Zero, Result[0], Result[1], Result[2], Result[3], Result[4], Result[5], Result[6], Result[7], Result[8], Result[9], Result[10], Result[11], Result[12], Result[13], Result[14], Result[15]);
endmodule

module PCDecoder (
  input  [3:0] Opcode,
  input  Subop,
  input  Zero,
  input  Less,
  output RegtoPC,
  output IMMtoPC,
  output ZerosToALU,
  output [3:0] ALUOp
);

  wire and_4_out, and_5_out, and_6_out, and_7_out, and_8_out, not_1_out, not_2_out, not_3_out, not_4_out,
       not_5_out, not_6_out, not_7_out, not_8_out, not_9_out, not_10_out, not_11_out, not_12_out, not_13_out,
       not_14_out, not_15_out, not_16_out;

  not not_1 (not_1_out, Opcode[2]);
  not not_2 (not_2_out, Opcode[1]);
  not not_3 (not_3_out, Subop);
  not not_4 (not_4_out, Opcode[2]);
  not not_5 (not_5_out, Opcode[1]);
  not not_6 (not_6_out, Opcode[0]);
  not not_7 (not_7_out, Opcode[2]);
  not not_8 (not_8_out, Opcode[1]);
  not not_9 (not_9_out, Zero);
  not not_10 (not_10_out, Opcode[2]);
  not not_11 (not_11_out, Zero);
  not not_12 (not_12_out, Opcode[0]);
  not not_13 (not_13_out, Zero);
  not not_14 (not_14_out, Less);
  not not_15 (not_15_out, Opcode[0]);
  and and_1 (ZerosToALU, Opcode[3], not_16_out);
  not not_16 (not_16_out, Opcode[2]);
  and and_2 (ALUOp[1], Opcode[3], not_1_out);
  and and_3 (RegtoPC, Opcode[3], Opcode[2], not_2_out, Opcode[0], not_3_out);
  and and_4 (and_4_out, Opcode[3], not_4_out, not_5_out, not_6_out, Zero);
  and and_5 (and_5_out, Opcode[3], not_7_out, not_8_out, Opcode[0], not_9_out);
  and and_6 (and_6_out, Opcode[3], not_10_out, Opcode[0], not_11_out, Less);
  and and_7 (and_7_out, Opcode[3], Opcode[1], not_12_out, not_13_out, not_14_out);
  and and_8 (and_8_out, Opcode[3], Opcode[2], Opcode[1], not_15_out);
  or or_1 (IMMtoPC, and_4_out, and_5_out, and_6_out, and_7_out, and_8_out);

  assign {ALUOp[3:2], ALUOp[0]} = 3'b000;
endmodule

module PCDecoderLogic (
  input  Opcode3,
  input  Opcode2,
  input  Opcode1,
  input  Opcode0,
  input  Subop,
  input  Zero,
  input  Less,
  output RegtoPC,
  output IMMtoPC,
  output OnestoALU
);

  wire and_2_out, and_3_out, and_4_out, and_5_out, and_6_out, not_1_out, not_2_out, not_3_out, not_4_out,
       not_5_out, not_6_out, not_7_out, not_8_out, not_9_out, not_10_out, not_11_out, not_12_out, not_13_out,
       not_14_out, not_15_out;

  not not_1 (not_1_out, Opcode1);
  not not_2 (not_2_out, Subop);
  not not_3 (not_3_out, Opcode2);
  not not_4 (not_4_out, Opcode1);
  not not_5 (not_5_out, Opcode0);
  not not_6 (not_6_out, Opcode2);
  not not_7 (not_7_out, Opcode1);
  not not_8 (not_8_out, Zero);
  not not_9 (not_9_out, Opcode2);
  not not_10 (not_10_out, Zero);
  not not_11 (not_11_out, Opcode0);
  not not_12 (not_12_out, Zero);
  not not_13 (not_13_out, Less);
  not not_14 (not_14_out, Opcode0);
  not not_15 (not_15_out, Opcode2);
  and and_1 (RegtoPC, Opcode3, Opcode2, not_1_out, Opcode0, not_2_out);
  and and_2 (and_2_out, Opcode3, not_3_out, not_4_out, not_5_out, Zero);
  and and_3 (and_3_out, Opcode3, not_6_out, not_7_out, Opcode0, not_8_out);
  and and_4 (and_4_out, Opcode3, not_9_out, Opcode0, not_10_out, Less);
  and and_5 (and_5_out, Opcode3, Opcode1, not_11_out, not_12_out, not_13_out);
  and and_6 (and_6_out, Opcode3, Opcode2, Opcode1, not_14_out);
  and and_7 (OnestoALU, Opcode3, not_15_out);
  or or_1 (IMMtoPC, and_2_out, and_3_out, and_4_out, and_5_out, and_6_out);
endmodule

module Decoder (
  input  [3:0] Opcode,
  input  Subop,
  input  Zero,
  input  Less,
  output ShiftSrc,
  output ShifterToReg,
  output RegWrite,
  output [3:0] ALUOp,
  output IMMtoALU,
  output RegtoPC,
  output IMMtoPC,
  output ZerosToALU,
  output MemWrite,
  output MemtoReg,
  output Halt,
  output LED,
  output WriteLED,
  output MemRead,
  output PCtoReg,
  output Sub
);

  wire Arith_LogDecoder_regwrite, JALDecoder_immtopc, JALDecoder_regwrite, MemDecoder_regwrite, or_1_out,
       PCDecoder_immtopc, ShifterDecoder_regwrite;
  wire [3:0] Arith_LogDecoder_aluoperation, PCDecoder_aluop;

  ShifterDecoder ShifterDecoder (
    .Opcode(Opcode), .ShiftSrc(ShiftSrc), .ShiftertoReg(ShifterToReg), .RegWrite(ShifterDecoder_regwrite));
  Arith_Log_Decoder Arith_LogDecoder (
    .Opcode(Opcode), .Subop(Subop), .ALUOperation(Arith_LogDecoder_aluoperation),
    .RegWrite(Arith_LogDecoder_regwrite), .ALUSrc(IMMtoALU));
  PCDecoder PCDecoder (
    .Opcode(Opcode), .Subop(Subop), .Zero(Zero), .Less(Less), .RegtoPC(RegtoPC), .IMMtoPC(PCDecoder_immtopc),
    .ZerosToALU(ZerosToALU), .ALUOp(PCDecoder_aluop));
  MemDecoder MemDecoder (
    .Opcode(Opcode), .Subop(Subop), .MemWrite(MemWrite), .MemtoReg(MemtoReg), .RegWrite(MemDecoder_regwrite),
    .MemRead(MemRead));
  HaltDecoder haltdecoder_1 (.Opcode(Opcode), .Halt(Halt), .LED(LED));
  PutDecoder PutDecoder (.Opcode(Opcode), .WriteLED(WriteLED));
  JALDecoder JALDecoder (
    .Opcode(Opcode), .IMMtoPC(JALDecoder_immtopc), .PCtoReg(PCtoReg), .RegWrite(JALDecoder_regwrite));
  and and_1 (Sub, ~Opcode[3], ~Opcode[2], Opcode[1], ~Opcode[0], ~Subop);  // AND_Gate
  or or_1 (or_1_out, ShifterDecoder_regwrite, Arith_LogDecoder_regwrite, MemDecoder_regwrite, JALDecoder_regwrite);
  or or_2 (IMMtoPC, PCDecoder_immtopc, JALDecoder_immtopc);
  assign ALUOp = Arith_LogDecoder_aluoperation | PCDecoder_aluop;  // OR_Gate or_3, 4 bits wide
  Multiplexer #(.enable("false")) multiplexer_1 (.in0(or_1_out), .in1(Sub), .out(RegWrite), .sel(Sub));
endmodule

module MemDecoder (
  input  [3:0] Opcode,
  input  Subop,
  output MemWrite,
  output MemtoReg,
  output RegWrite,
  output MemRead
);

  and and_1 (MemWrite, ~Opcode[0], Opcode[1], Opcode[2], ~Opcode[3], Subop);  // AND_Gate
  and and_2 (MemRead, ~Opcode[0], Opcode[1], Opcode[2], ~Opcode[3], ~Subop);  // AND_Gate

  assign MemtoReg = MemRead;
  assign RegWrite = MemRead;
endmodule

module HaltDecoder (
  input  [3:0] Opcode,
  output Halt,
  output LED
);

  and and_1 (Halt, ~Opcode[3], Opcode[2], Opcode[1], Opcode[0]);  // AND_Gate

  assign LED = Halt;
endmodule

module PutDecoder (
  input  [3:0] Opcode,
  output WriteLED
);

  and and_1 (WriteLED, Opcode[0], Opcode[1], Opcode[2], Opcode[3]);
endmodule

module JALDecoder (
  input  [3:0] Opcode,
  output IMMtoPC,
  output PCtoReg,
  output RegWrite
);

  and and_1 (IMMtoPC, ~Opcode[0], ~Opcode[1], Opcode[2], Opcode[3]);  // AND_Gate

  assign PCtoReg = IMMtoPC;
  assign RegWrite = IMMtoPC;
endmodule

module ResultToLess (
  input  [15:0] Result,
  output Less
);


  assign Less = Result[15];
endmodule

module side (
  input  Op3,
  input  Op2,
  input  Op1,
  input  Op0,
  output Op3_2,
  output Op2_2,
  output Op1_2,
  output Op0_2
);

  wire not_1_out;

  and and_1 (Op1_2, Op3, not_1_out);
  not not_1 (not_1_out, Op2);

  assign Op0_2 = 1'b0;
  assign Op2_2 = 1'b0;
  assign Op3_2 = 1'b0;
endmodule

module IF_ID (
  input  [7:0] PC_1,
  input  [7:0] PC,
  input  enableReg,
  input  [15:0] instruction,
  input  reset,
  input  clock,
  input  enable,
  output [7:0] PC_1_2,
  output [7:0] PC_2,
  output enableReg_2,
  output [15:0] instruction_2
);

  Register register_1 (.D(PC_1), .en(enable), .Q(PC_1_2), .clk(clock), .clr(1'b0));
  Register register_2 (.D(PC), .en(enable), .Q(PC_2), .clk(clock), .clr(1'b0));
  Register #(.width(1)) register_3 (.D(enableReg), .en(enable), .Q(enableReg_2), .clk(clock));  // open: clr
  Register #(.width(16)) register_4 (.D(instruction), .en(enable), .Q(instruction_2), .clk(clock), .clr(reset));
endmodule

module ID_EX (
  input  [7:0] PC_1,
  input  [7:0] PC,
  input  [15:0] rd1,
  input  [15:0] rd2,
  input  regEnable,
  input  [15:0] sign_extend,
  input  [2:0] rr1,
  input  [2:0] rr2,
  input  [3:0] ALUOp,
  input  IMMTOALU,
  input  REGTOPC,
  input  IMMTOPC,
  input  ZEROESTOPC,
  input  MEMWRITE,
  input  MEMTOREG,
  input  WRITELED,
  input  MEMREAD,
  input  REGWRITE,
  input  SUB,
  input  enable,
  input  reset,
  input  clock,
  output [7:0] PC_1_2,
  output [7:0] PC_2,
  output [15:0] rd1_2,
  output [15:0] rd2_2,
  output regEnable_2,
  output [15:0] sign_extend_2,
  output [2:0] rr1_2,
  output [2:0] rr2_2,
  output [3:0] ALUOp_2,
  output IMMTOALU_2,
  output REGTOPC_2,
  output IMMTOPC_2,
  output ZEROESTOPC_2,
  output MEMWRITE_2,
  output MEMTOREG_2,
  output WRITELED_2,
  output MEMREAD_2,
  output REGWRITE_2,
  output SUB_2
);

  Register #(.width(3)) register_1 (.D(rr2), .en(enable), .Q(rr2_2), .clk(clock));  // open: clr
  Register register_2 (.D(PC_1), .en(enable), .Q(PC_1_2), .clk(clock), .clr(reset));
  Register register_3 (.D(PC), .en(enable), .Q(PC_2), .clk(clock), .clr(reset));
  Register #(.width(16)) register_4 (.D(rd1), .en(enable), .Q(rd1_2), .clk(clock), .clr(reset));
  Register #(.width(16)) register_5 (.D(rd2), .en(enable), .Q(rd2_2), .clk(clock), .clr(reset));
  Register #(.width(1)) register_6 (.D(regEnable), .en(enable), .Q(regEnable_2), .clk(clock), .clr(reset));
  Register #(.width(16)) register_7 (.D(sign_extend), .en(enable), .Q(sign_extend_2), .clk(clock), .clr(reset));
  Register #(.width(3)) register_8 (.D(rr1), .en(enable), .Q(rr1_2), .clk(clock), .clr(reset));
  Register #(.width(4)) register_9 (.D(ALUOp), .en(enable), .Q(ALUOp_2), .clk(clock), .clr(reset));
  Register #(.width(1)) register_10 (.D(IMMTOALU), .en(enable), .Q(IMMTOALU_2), .clk(clock), .clr(reset));
  Register #(.width(1)) register_11 (.D(REGTOPC), .en(enable), .Q(REGTOPC_2), .clk(clock), .clr(reset));
  Register #(.width(1)) register_12 (.D(IMMTOPC), .en(enable), .Q(IMMTOPC_2), .clk(clock), .clr(reset));
  Register #(.width(1)) register_13 (.D(ZEROESTOPC), .en(enable), .Q(ZEROESTOPC_2), .clk(clock), .clr(reset));
  Register #(.width(1)) register_14 (.D(MEMWRITE), .en(enable), .Q(MEMWRITE_2), .clk(clock), .clr(reset));
  Register #(.width(1)) register_15 (.D(MEMTOREG), .en(enable), .Q(MEMTOREG_2), .clk(clock), .clr(reset));
  Register #(.width(1)) register_16 (.D(WRITELED), .en(enable), .Q(WRITELED_2), .clk(clock), .clr(reset));
  Register #(.width(1)) register_17 (.D(MEMREAD), .en(enable), .Q(MEMREAD_2), .clk(clock), .clr(reset));
  Register #(.width(1)) register_18 (.D(REGWRITE), .en(enable), .Q(REGWRITE_2), .clk(clock), .clr(reset));
  Register #(.width(1)) register_19 (.D(SUB), .en(enable), .Q(SUB_2), .clk(clock), .clr(reset));
endmodule

module EX_MEM (
  input  [15:0] putValue,
  input  [15:0] ALU_result,
  input  [15:0] write_data,
  input  [2:0] rr1_rd,
  input  MEMWRITE,
  input  MEMTOREG,
  input  MEMREAD,
  input  writeLED,
  input  REGWRITE,
  input  regEnable,
  input  enable,
  input  clock,
  output [15:0] putValue_2,
  output [15:0] ALU_result_2,
  output [15:0] write_data_2,
  output [2:0] rr1_rd_2,
  output MEMWRITE_2,
  output MEMTOREG_2,
  output MEMREAD_2,
  output writeLE,
  output REGWRITE_2,
  output regEnable_2
);

  wire undriven, undriven_2, undriven_3;

  Register #(.width(1)) register_1 (.D(writeLED), .en(enable), .Q(writeLE), .clk(clock));  // open: clr
  Register #(.width(16)) register_2 (.D(putValue), .en(enable), .Q(putValue_2), .clk(clock), .clr(undriven));
  Register #(.width(16)) register_3 (.D(ALU_result), .en(enable), .Q(ALU_result_2), .clk(clock), .clr(undriven));
  Register #(.width(16)) register_4 (.D(write_data), .en(enable), .Q(write_data_2), .clk(clock), .clr(undriven));
  Register #(.width(3)) register_5 (.D(rr1_rd), .en(enable), .Q(rr1_rd_2), .clk(clock), .clr(undriven));
  Register #(.width(1)) register_6 (.D(MEMWRITE), .en(enable), .Q(MEMWRITE_2), .clk(clock), .clr(undriven));
  Register #(.width(1)) register_7 (.D(MEMTOREG), .en(enable), .Q(MEMTOREG_2), .clk(clock), .clr(undriven));
  Register #(.width(1)) register_8 (.D(MEMREAD), .en(enable), .Q(MEMREAD_2), .clk(clock), .clr(undriven));
  Register #(.width(1)) register_9 (.D(REGWRITE), .en(enable), .Q(REGWRITE_2), .clk(clock), .clr(undriven_2));
  Register #(.width(1)) register_10 (.D(regEnable), .en(enable), .Q(regEnable_2), .clk(clock), .clr(undriven_3));
endmodule

module MEM_WB (
  input  [15:0] put_value,
  input  [15:0] read_data,
  input  [15:0] address,
  input  [2:0] rd_rs,
  input  MEMTOREG,
  input  REGWRITE,
  input  writeLED,
  input  enable,
  input  reset,
  input  clock,
  output [15:0] putvalue,
  output [15:0] read_data_2,
  output [15:0] address_2,
  output [2:0] rd_rs_2,
  output MEMTOREG_2,
  output REGWRITE_2,
  output writeLED_2
);

  Register #(.width(1)) register_1 (.D(writeLED), .en(enable), .Q(writeLED_2), .clk(clock));  // open: clr
  Register #(.width(16)) register_2 (.D(put_value), .en(enable), .Q(putvalue), .clk(clock));  // open: clr
  Register #(.width(16)) register_3 (.D(read_data), .en(enable), .Q(read_data_2), .clk(clock), .clr(reset));
  Register #(.width(16)) register_4 (.D(address), .en(enable), .Q(address_2), .clk(clock), .clr(reset));
  Register #(.width(3)) register_5 (.D(rd_rs), .en(enable), .Q(rd_rs_2), .clk(clock), .clr(reset));
  Register #(.width(1)) register_6 (.D(MEMTOREG), .en(enable), .Q(MEMTOREG_2), .clk(clock), .clr(reset));
  Register #(.width(1)) register_7 (.D(REGWRITE), .en(enable), .Q(REGWRITE_2), .clk(clock), .clr(reset));
endmodule

module Forwarding_Unit (
  input  [2:0] EX_MEM_registerRd,
  input  [2:0] MEM_WB_registerRd,
  input  [2:0] ID_EX_registerRs1,
  input  [2:0] ID_EX_registerRs2,
  input  EX_MEM_regWrite,
  input  MEM_WB_regWrite,
  output [1:0] controlA,
  output [1:0] controlB
);

  wire comparator_1_eq, comparator_2_eq, comparator_3_eq, comparator_4_eq, or_1_out, or_2_out;
  wire [1:0] and_1_out, and_2_out;

  Comparator #(.width(3)) comparator_1 (
    .a(EX_MEM_registerRd), .b(ID_EX_registerRs1), .eq(comparator_1_eq));  // open: gt, lt
  or or_1 (or_1_out, ID_EX_registerRs1[0], ID_EX_registerRs1[1], ID_EX_registerRs1[2]);
  or or_2 (or_2_out, ID_EX_registerRs2[0], ID_EX_registerRs2[1], ID_EX_registerRs2[2]);
  and and_1 (and_1_out[0], comparator_1_eq, or_1_out, EX_MEM_regWrite);
  Comparator #(.width(3)) comparator_2 (
    .a(EX_MEM_registerRd), .b(ID_EX_registerRs2), .eq(comparator_2_eq));  // open: gt, lt
  Comparator #(.width(3)) comparator_3 (
    .a(MEM_WB_registerRd), .b(ID_EX_registerRs1), .eq(comparator_3_eq));  // open: gt, lt
  Comparator #(.width(3)) comparator_4 (
    .a(MEM_WB_registerRd), .b(ID_EX_registerRs2), .eq(comparator_4_eq));  // open: gt, lt
  and and_2 (and_2_out[0], comparator_2_eq, or_2_out, EX_MEM_regWrite);
  and and_3 (and_1_out[1], MEM_WB_regWrite, or_1_out, comparator_3_eq);
  and and_4 (and_2_out[1], MEM_WB_regWrite, or_2_out, comparator_4_eq);
  Multiplexer #(.select(2), .width(2), .enable("false")) multiplexer_1 (
    .in0(2'b00), .in1(2'b10), .in2(2'b01), .out(controlA), .sel(and_1_out));  // open: in3
  Multiplexer #(.select(2), .width(2), .enable("false")) multiplexer_2 (
    .in0(2'b00), .in1(2'b10), .in2(2'b01), .out(controlB), .sel(and_2_out));  // open: in3

  // Notes on the sheet:
  //   set A to 10
  //   set B to 10
  //   set A to 01
  //   set B to 01
  //   control A
  //   control B
endmodule

module regWriteReset (
  input  [7:0] in_1,
  input  [7:0] in_2,
  output out_3
);

  and and_1 (out_3, in_1[0], ~in_1[1], ~in_1[2], ~in_1[3], ~in_1[4], ~in_1[5], ~in_1[6], ~in_1[7], ~in_2[0], ~in_2[1], ~in_2[2], ~in_2[3], ~in_2[4], ~in_2[5], ~in_2[6], ~in_2[7]);  // AND_Gate
endmodule

module pcSelect (
  input  [7:0] PC_1,
  input  [7:0] immediate,
  input  IMMTOPC,
  input  [15:0] rd1,
  input  REGTOPC,
  output [7:0] out_6
);

  wire [7:0] multiplexer_1_out, RegistertoAddress_address;

  Multiplexer #(.width(8), .enable("false")) multiplexer_1 (
    .in0(PC_1), .in1(immediate), .out(multiplexer_1_out), .sel(IMMTOPC));
  ALUtoPC RegistertoAddress (.ALUOut(rd1), .Address(RegistertoAddress_address));
  Multiplexer #(.width(8), .enable("false")) multiplexer_2 (
    .in0(multiplexer_1_out), .in1(RegistertoAddress_address), .out(out_6), .sel(REGTOPC));
endmodule

module Data_Hazard (
  input  [15:0] inst,
  input  clock,
  input  halt,
  output [15:0] mux_out,
  output or_out
);

  wire and_1_out, and_2_out, and_3_out, and_4_out, and_5_out, not_1_out, not_2_out, or_1_out, register_1_q;

  and and_1 (and_1_out, ~mux_out[12], ~mux_out[14]);  // AND_Gate
  and and_2 (and_2_out, ~mux_out[13], mux_out[15]);  // AND_Gate
  and and_3 (and_3_out, mux_out[13], mux_out[15]);
  or or_1 (or_1_out, and_2_out, and_3_out);
  and and_4 (and_4_out, and_1_out, or_1_out);
  Register #(.width(1)) register_1 (.D(and_4_out), .en(1'b1), .Q(register_1_q), .clk(clock));  // open: clr
  not not_1 (not_1_out, and_4_out);
  not not_2 (not_2_out, halt);
  Multiplexer #(.width(16), .enable("false")) multiplexer_1 (
    .in0(inst), .in1(16'h1000), .out(mux_out), .sel(register_1_q));
  and and_5 (and_5_out, not_1_out, not_2_out);
  or or_2 (or_out, register_1_q, and_5_out);
endmodule
